// Logisim project v2.8.4.circ as structural Verilog
module bus_test (
  input  Ram_B_OE,
  input  Ram_B_WE,
  input  Ram_sys_OE,
  input  Ram_sys_WE,
  input  Ram_A_OE,
  input  Ram_A_WE,
  input  Ram_inst_OE,
  input  Ram_inst_input_enable,
  input  MBR_B_CB,
  input  MBR_A_CB,
  input  MBR_Z_CB,
  input  MBR_B_WE,
  input  MBR_A_WE,
  input  MBR_Z_WE,
  input  MAR_B_WE,
  input  MAR_A_WE,
  input  MAR_Z_WE,
  input  Reg_8_WE,
  input  Reg_7_WE,
  input  [4:0] in_20,
  input  Reg_6_WE,
  input  Reg_5_WE,
  input  Reg_4_WE,
  input  Reg_3_WE,
  input  Reg_2_WE,
  input  Reg_1_WE,
  input  Reg_8_OE,
  input  Reg_7_OE,
  input  Reg_6_OE,
  input  Reg_5_OE,
  input  Reg_4_OE,
  input  Reg_3_OE,
  input  Reg_2_OE,
  input  Reg_1_OE,
  input  Inst_splitter_WE,
  input  Reset,
  input  count_increment_on,
  input  count_reset,
  input  Opcode_Reg_WE,
  input  Add_on,
  input  Reg_ALU_out_WE
);

  wire alu_1_store, block_store_incrementer_1_opcode_on, busterminus_1_adda_rama, busterminus_1_adda_ramb,
       busterminus_1_mem_swap, busterminus_1_move, busterminus_1_move_flag, clock_1_out,
       controlled_buffer_20_out, halt_1_halt_inst, matmult_1_opcode_on, not_1_out, not_2_out, not_3_out,
       not_4_out, or_1_out, or_2_out, reg_bank_a_1_reg_swap, split_1_flag;
  wire [4:0] block_incrementer_1_inc_add, block_incrementer_2_inc_add, block_store_incrementer_1_inc_add,
       busterminus_1_add_a_out, busterminus_1_add_b_out, controlled_buffer_3_out, controlled_buffer_7_out,
       controlled_buffer_8_out, controlled_buffer_22_out, counter_1_q, MAR_A_q, MAR_B_q, MAR_Zero_q,
       split_1_add_a, split_1_add_b, split_1_opcode;
  wire [4:4] register_2_q;
  wire [7:0] register_2_q_2;
  wire [15:0] alu_1_result, alu_1_sto_overflow, busterminus_1_data_ab_out, busterminus_1_data_sysa_out,
       controlled_buffer_1_out, controlled_buffer_2_out, controlled_buffer_5_out, controlled_buffer_9_out,
       controlled_buffer_13_out, controlled_buffer_14_out, controlled_buffer_23_out, matmult_1_ae_bg,
       MBR_A_q, MBR_B_q, MBR_Z_q, ram_1_dout, ram_2_dout, ram_3_dout, ram_4_dout, reg_bank_a_1_data_out,
       reg_bank_a_1_reg1_out, reg_bank_a_1_reg2_out, reg_bank_a_1_reg3_out, reg_bank_a_1_reg4_out,
       reg_bank_b_1_data_out, reg_bank_b_1_reg5_out, reg_bank_b_1_reg6_out, reg_bank_b_1_reg7_out,
       reg_bank_b_1_reg8_out;
  wire [39:0] rom_1_data;

  // Probe on reg_bank_b_1_data_out
  // Probe on reg_bank_a_1_data_out
  ALU alu_1 (
    .A(reg_bank_a_1_data_out), .B(reg_bank_b_1_data_out), .opcode({register_2_q[4], register_2_q_2[7:4]}),
    .flag(split_1_flag), .Result(alu_1_result), .store(alu_1_store), .sto_overflow(alu_1_sto_overflow));
  assign controlled_buffer_1_out = matmult_1_opcode_on ? matmult_1_ae_bg : 16'bz;  // Controlled_Buffer controlled_buffer_1
  matmult matmult_1 (
    .OPcode({register_2_q[4], register_2_q_2[7:4]}), .Flag(split_1_flag), .a(reg_bank_a_1_reg1_out),
    .b(reg_bank_a_1_reg2_out), .c(reg_bank_a_1_reg3_out), .d(reg_bank_a_1_reg4_out),
    .e(reg_bank_b_1_reg5_out), .f(reg_bank_b_1_reg6_out), .g(reg_bank_b_1_reg7_out),
    .h(reg_bank_b_1_reg8_out), .Clock(controlled_buffer_20_out), .AE_BG(matmult_1_ae_bg),
    .AF_BH(matmult_1_ae_bg), .CE_DG(matmult_1_ae_bg), .CF_DH(matmult_1_ae_bg),
    .AE_BG_Overflow(matmult_1_ae_bg), .AF_BH_Overflow(matmult_1_ae_bg), .CE_DG_Overflow(matmult_1_ae_bg),
    .CF_DH_Overflow(matmult_1_ae_bg), .Opcode_on(matmult_1_opcode_on));
  // Probe on alu_1_result
  Register #(.width(16)) register_1 (
    .D(alu_1_result), .en(rom_1_data[0]), .clk(controlled_buffer_20_out), .Q(alu_1_sto_overflow));  // open: clr
  // Probe on alu_1_sto_overflow
  assign controlled_buffer_2_out = alu_1_store ? alu_1_sto_overflow : 16'bz;  // Controlled_Buffer controlled_buffer_2
  Register #(.width(5)) register_2 (
    .D(split_1_opcode), .en(rom_1_data[2]), .clk(controlled_buffer_20_out),
    .Q({register_2_q[4], register_2_q_2[7:4]}), .clr(rom_1_data[5]));
  Counter #(.max('h1f), .width(5)) counter_1 (
    .up(rom_1_data[4]), .count(rom_1_data[4]), .clk(controlled_buffer_20_out), .Q(counter_1_q));  // open: clr, load, D, carry
  Reg_bank_A reg_bank_a_1 (
    .data_in(controlled_buffer_1_out), .Clock(controlled_buffer_20_out),
    .OPcode({register_2_q[4], register_2_q_2[7:4]}), .Flag(split_1_flag), .Reg1_WE(rom_1_data[15]),
    .Reg2_WE(rom_1_data[16]), .Reg3_WE(rom_1_data[17]), .Reg4_WE(rom_1_data[18]), .Address(MAR_A_q),
    .Reg1_CB(rom_1_data[7]), .Reg2_CB(rom_1_data[8]), .Reg3_CB(rom_1_data[9]), .Reg4_CB(rom_1_data[10]),
    .data_out(reg_bank_a_1_data_out), .Block_store(controlled_buffer_2_out),
    .Reg1_out(reg_bank_a_1_reg1_out), .Reg2_out(reg_bank_a_1_reg2_out), .Reg3_out(reg_bank_a_1_reg3_out),
    .Reg4_out(reg_bank_a_1_reg4_out), .Reg_swap(reg_bank_a_1_reg_swap));  // open: Reg_Reset
  assign controlled_buffer_3_out = not_1_out ? counter_1_q : 5'bz;  // Controlled_Buffer controlled_buffer_3
  not not_1 (not_1_out, block_store_incrementer_1_opcode_on);
  assign controlled_buffer_1_out = reg_bank_a_1_reg_swap ? reg_bank_b_1_data_out : 16'bz;  // Controlled_Buffer controlled_buffer_4
  assign controlled_buffer_5_out = reg_bank_a_1_reg_swap ? reg_bank_a_1_data_out : 16'bz;  // Controlled_Buffer controlled_buffer_5
  split split_1 (
    .Instruction(MBR_Z_q), .write_enable(rom_1_data[6]), .Clock(controlled_buffer_20_out),
    .reset(rom_1_data[5]), .Add_B(split_1_add_b), .Add_A(split_1_add_a), .Opcode(split_1_opcode),
    .flag(split_1_flag));
  Busterminus busterminus_1 (
    .Opcode({register_2_q[4], register_2_q_2[7:4]}), .Flag(split_1_flag), .Clock(controlled_buffer_20_out),
    .Add_B(MAR_B_q), .Add_A(MAR_A_q), .Data_sys(MBR_Z_q), .Data_A(MBR_A_q), .Data_B(MBR_B_q),
    .Add_B_out(busterminus_1_add_b_out), .Add_A_out(busterminus_1_add_a_out),
    .AddA_RamA(busterminus_1_adda_rama), .AddA_RamB(busterminus_1_adda_ramb),
    .Data_AB_Out(busterminus_1_data_ab_out), .Data_SysA_Out(busterminus_1_data_sysa_out),
    .Mem_swap(busterminus_1_mem_swap), .Move_flag(busterminus_1_move_flag), .Move(busterminus_1_move));
  not not_2 (not_2_out, rom_1_data[1]);
  Reg_bank_B reg_bank_b_1 (
    .Data_in(controlled_buffer_5_out), .Clock(controlled_buffer_20_out),
    .Opcode({register_2_q[4], register_2_q_2[7:4]}), .Flag(split_1_flag), .Reg5_WE(rom_1_data[19]),
    .Reg6_WE(rom_1_data[20]), .Reg7_WE(rom_1_data[21]), .Reg8_WE(rom_1_data[22]), .Address(MAR_B_q),
    .Reg5_CB(rom_1_data[11]), .Reg6_CB(rom_1_data[12]), .Reg7_CB(rom_1_data[13]), .Reg8_CB(rom_1_data[14]),
    .Data_out(reg_bank_b_1_data_out), .Block_store(controlled_buffer_2_out),
    .Reg5_out(reg_bank_b_1_reg5_out), .Reg6_out(reg_bank_b_1_reg6_out), .Reg7_out(reg_bank_b_1_reg7_out),
    .Reg8_out(reg_bank_b_1_reg8_out));  // open: Reg_reset
  block_store_incrementer block_store_incrementer_1 (
    .OPcode({register_2_q[4], register_2_q_2[7:4]}), .Address(controlled_buffer_3_out),
    .Clock(controlled_buffer_20_out), .inc_add(block_store_incrementer_1_inc_add),
    .Opcode_on(block_store_incrementer_1_opcode_on));
  assign controlled_buffer_3_out = block_store_incrementer_1_opcode_on ? MAR_A_q : 5'bz;  // Controlled_Buffer controlled_buffer_6
  assign controlled_buffer_7_out = not_2_out ? block_incrementer_1_inc_add : 5'bz;  // Controlled_Buffer controlled_buffer_7
  block_incrementer block_incrementer_1 (
    .OPcode({register_2_q[4], register_2_q_2[7:4]}), .Address(split_1_add_a),
    .Clock(controlled_buffer_20_out), .inc_add(block_incrementer_1_inc_add));
  assign controlled_buffer_8_out = not_2_out ? block_incrementer_2_inc_add : 5'bz;  // Controlled_Buffer controlled_buffer_8
  block_incrementer block_incrementer_2 (
    .OPcode({register_2_q[4], register_2_q_2[7:4]}), .Address(split_1_add_b),
    .Clock(controlled_buffer_20_out), .inc_add(block_incrementer_2_inc_add));
  assign controlled_buffer_9_out = not_3_out ? busterminus_1_data_sysa_out : 16'bz;  // Controlled_Buffer controlled_buffer_9
  not not_3 (not_3_out, busterminus_1_mem_swap);
  assign controlled_buffer_9_out = busterminus_1_mem_swap ? busterminus_1_data_ab_out : 16'bz;  // Controlled_Buffer controlled_buffer_10
  or or_1 (or_1_out, busterminus_1_mem_swap, busterminus_1_move);
  or or_2 (or_2_out, busterminus_1_mem_swap, busterminus_1_move_flag);
  assign busterminus_1_add_b_out = not_2_out ? block_store_incrementer_1_inc_add : 5'bz;  // Controlled_Buffer controlled_buffer_11
  assign controlled_buffer_8_out = busterminus_1_adda_ramb ? busterminus_1_add_a_out : 5'bz;  // Controlled_Buffer controlled_buffer_12
  assign controlled_buffer_13_out = or_1_out ? controlled_buffer_9_out : 16'bz;  // Controlled_Buffer controlled_buffer_13
  assign controlled_buffer_14_out = or_2_out ? busterminus_1_data_sysa_out : 16'bz;  // Controlled_Buffer controlled_buffer_14
  halt halt_1 (.flag(split_1_flag), .Opcode({register_2_q[4], register_2_q_2[7:4]}), .halt_inst(halt_1_halt_inst));
  Register #(.width(5)) MAR_Zero (
    .D(busterminus_1_add_b_out), .en(rom_1_data[23]), .clk(controlled_buffer_20_out), .Q(MAR_Zero_q));  // open: clr
  Register #(.width(5)) MAR_A (
    .D(controlled_buffer_7_out), .en(rom_1_data[24]), .clk(controlled_buffer_20_out), .Q(MAR_A_q));  // open: clr
  assign controlled_buffer_7_out = busterminus_1_adda_rama ? busterminus_1_add_a_out : 5'bz;  // Controlled_Buffer controlled_buffer_15
  Register #(.width(5)) MAR_B (
    .D(controlled_buffer_8_out), .en(rom_1_data[25]), .clk(controlled_buffer_20_out), .Q(MAR_B_q));  // open: clr
  Register #(.width(16)) MBR_Z (
    .D(controlled_buffer_2_out), .en(rom_1_data[26]), .clk(controlled_buffer_20_out), .Q(MBR_Z_q));  // open: clr
  assign controlled_buffer_1_out = rom_1_data[30] ? MBR_A_q : 16'bz;  // Controlled_Buffer controlled_buffer_16
  Register #(.width(16)) MBR_A (
    .D(controlled_buffer_13_out), .en(rom_1_data[27]), .clk(controlled_buffer_20_out), .Q(MBR_A_q));  // open: clr
  assign controlled_buffer_5_out = rom_1_data[31] ? MBR_B_q : 16'bz;  // Controlled_Buffer controlled_buffer_17
  Register #(.width(16)) MBR_B (
    .D(controlled_buffer_14_out), .en(rom_1_data[28]), .clk(controlled_buffer_20_out), .Q(MBR_B_q));  // open: clr
  assign controlled_buffer_2_out = rom_1_data[29] ? controlled_buffer_23_out : 16'bz;  // Controlled_Buffer controlled_buffer_18
  assign controlled_buffer_13_out = rom_1_data[30] ? ram_2_dout : 16'bz;  // Controlled_Buffer controlled_buffer_19
  Clock clock_1 (.out(clock_1_out));
  assign controlled_buffer_20_out = halt_1_halt_inst ? clock_1_out : 1'bz;  // Controlled_Buffer controlled_buffer_20
  assign controlled_buffer_14_out = rom_1_data[31] ? ram_4_dout : 16'bz;  // Controlled_Buffer controlled_buffer_21
  assign controlled_buffer_22_out = rom_1_data[32] ? MAR_Zero_q : 5'bz;  // Controlled_Buffer controlled_buffer_22
  RAM #(.addrWidth(5), .dataWidth(16), .\type ("nonvolatile")) ram_1 (
    .addr(controlled_buffer_22_out), .oe(rom_1_data[33]), .clk(controlled_buffer_20_out), .dout(ram_1_dout));  // open: we, din
  RAM #(.addrWidth(5), .dataWidth(16)) ram_2 (
    .addr(MAR_A_q), .we(rom_1_data[34]), .oe(rom_1_data[35]), .clk(controlled_buffer_20_out), .din(MBR_A_q),
    .dout(ram_2_dout));
  // Probe on ram_1_dout
  assign controlled_buffer_23_out = not_4_out ? ram_1_dout : 16'bz;  // Controlled_Buffer controlled_buffer_23
  not not_4 (not_4_out, rom_1_data[37]);
  assign controlled_buffer_23_out = rom_1_data[37] ? ram_3_dout : 16'bz;  // Controlled_Buffer controlled_buffer_24
  // Probe on ram_2_dout
  RAM #(.addrWidth(5), .dataWidth(16), .\type ("nonvolatile")) ram_3 (
    .addr(MAR_Zero_q), .we(rom_1_data[36]), .oe(rom_1_data[37]), .clk(controlled_buffer_20_out),
    .din(MBR_Z_q), .dout(ram_3_dout));
  RAM #(.addrWidth(5), .dataWidth(16)) ram_4 (
    .addr(MAR_B_q), .we(rom_1_data[38]), .oe(rom_1_data[39]), .clk(controlled_buffer_20_out), .din(MBR_B_q),
    .dout(ram_4_dout));
  // Probe on ram_4_dout
  ROM #(.dataWidth(40)) rom_1 (.addr(register_2_q_2), .data(rom_1_data));
  Counter #(.max('hf), .width(4)) counter_2 (
    .clr(rom_1_data[3]), .up(1'b1), .count(1'b1), .clk(controlled_buffer_20_out), .Q(register_2_q_2[3:0]));  // open: load, D, carry

  // Notes on the sheet:
  //   B
  //   A
  //   Instruction Ram
  //   Ram_A
  //   System Ram
  //   Ram_B
  //   contents of rom_1 (hex, n*v repeats v):
  //   1e3800884 3e0000880 1e4000880 1e00008c0 1e3000888 12*0 89e0000880 1f8000880 1e0088880 1e0000891
  //   1e00008a8 27*0 89e0000880 1f8000880 1e0088880 1e0000891 1e00008a8 11*0 1c4000880 11c4000890
  //   1c00008a8 13*0 89e0000000 1f8000000 100000000 118000000 4500000010 28 10*0 120000010 120000028 14*0
  //   4*89fb088000 89fb110000 89fb110000 89fb220000 89fb220000 89fb440000 89fb440010 1e0000028 5*0
  //   c4800880 10c4801100 10c4802200 10c4804400 10c4800010 10c0800028 11*0 8000 10000 20000 40010 28 10*0
  //   89e0000880 1f8000880 1e0088880 1e0000891 1e00008a8 11*0 89e0000880 1f8000880 1e0088880 1e0000891
  //   1e00008a8 11*0 89e0000880 1f8000880 1e0088880 1e0000891 1e00008a8 11*0 89e0000880 1f8000880
  //   1e0088880 1e0000891 1e00008a8 11*0 10 28 15*0 2020800002 2024000002 2024000002 2027000002 2020000002
  //   2038800002 6420000012 202000002a
endmodule

module Reg_bank_A (
  input  [15:0] data_in,
  input  Clock,
  input  [4:0] OPcode,
  input  Flag,
  input  Reg1_WE,
  input  Reg2_WE,
  input  Reg3_WE,
  input  Reg4_WE,
  input  [4:0] Address,
  input  Reg1_CB,
  input  Reg2_CB,
  input  Reg3_CB,
  input  Reg4_CB,
  input  Reg_Reset,
  output [15:0] data_out,
  output [15:0] Block_store,
  output [15:0] Reg1_out,
  output [15:0] Reg2_out,
  output [15:0] Reg3_out,
  output [15:0] Reg4_out,
  output Reg_swap
);

  wire and_2_out, and_3_out, and_4_out, and_5_out, and_6_out, and_7_out, controlled_buffer_1_out,
       controlled_buffer_2_out, controlled_buffer_3_out, controlled_buffer_4_out, controlled_buffer_5_out,
       controlled_buffer_6_out, controlled_buffer_7_out, controlled_buffer_8_out, not_1_out, not_2_out,
       not_3_out, not_4_out, not_5_out, not_6_out, not_7_out, not_8_out, not_9_out, not_10_out, not_11_out,
       not_12_out, not_13_out, not_14_out, not_15_out, not_16_out;
  wire [15:0] Reg1_q, Reg2_q, Reg3_q, Reg4_q;

  not not_1 (not_1_out, Address[0]);
  not not_2 (not_2_out, Address[1]);
  not not_3 (not_3_out, Address[2]);
  not not_4 (not_4_out, Address[3]);
  not not_5 (not_5_out, Address[4]);
  not not_6 (not_6_out, OPcode[0]);
  not not_7 (not_7_out, OPcode[3]);
  not not_8 (not_8_out, OPcode[4]);
  assign controlled_buffer_1_out = Reg_swap ? controlled_buffer_5_out : 1'bz;  // Controlled_Buffer controlled_buffer_1
  assign controlled_buffer_2_out = Reg_swap ? controlled_buffer_6_out : 1'bz;  // Controlled_Buffer controlled_buffer_2
  assign controlled_buffer_3_out = Reg_swap ? controlled_buffer_7_out : 1'bz;  // Controlled_Buffer controlled_buffer_3
  assign controlled_buffer_4_out = Reg_swap ? controlled_buffer_8_out : 1'bz;  // Controlled_Buffer controlled_buffer_4
  and and_1 (Reg_swap, not_6_out, OPcode[1], OPcode[2], not_7_out, not_8_out);
  and and_2 (and_2_out, Address[0], not_2_out, not_3_out, not_4_out, not_5_out);
  and and_3 (and_3_out, not_1_out, Address[1], not_3_out, not_4_out, not_5_out);
  and and_4 (and_4_out, Address[0], Address[1], not_3_out, not_4_out, not_5_out);
  and and_5 (and_5_out, not_1_out, not_2_out, Address[2], not_4_out, not_5_out);
  not not_9 (not_9_out, Reg_swap);
  assign controlled_buffer_5_out = Reg_swap ? and_2_out : 1'bz;  // Controlled_Buffer controlled_buffer_5
  assign controlled_buffer_6_out = Reg_swap ? and_3_out : 1'bz;  // Controlled_Buffer controlled_buffer_6
  assign controlled_buffer_7_out = Reg_swap ? and_4_out : 1'bz;  // Controlled_Buffer controlled_buffer_7
  assign controlled_buffer_8_out = Reg_swap ? and_5_out : 1'bz;  // Controlled_Buffer controlled_buffer_8
  assign controlled_buffer_1_out = not_9_out ? Reg1_WE : 1'bz;  // Controlled_Buffer controlled_buffer_9
  assign controlled_buffer_2_out = not_9_out ? Reg2_WE : 1'bz;  // Controlled_Buffer controlled_buffer_10
  assign controlled_buffer_3_out = not_9_out ? Reg3_WE : 1'bz;  // Controlled_Buffer controlled_buffer_11
  assign controlled_buffer_4_out = not_9_out ? Reg4_WE : 1'bz;  // Controlled_Buffer controlled_buffer_12
  assign controlled_buffer_5_out = not_9_out ? Reg1_CB : 1'bz;  // Controlled_Buffer controlled_buffer_13
  assign controlled_buffer_6_out = not_9_out ? Reg2_CB : 1'bz;  // Controlled_Buffer controlled_buffer_14
  assign controlled_buffer_7_out = not_9_out ? Reg3_CB : 1'bz;  // Controlled_Buffer controlled_buffer_15
  assign controlled_buffer_8_out = not_9_out ? Reg4_CB : 1'bz;  // Controlled_Buffer controlled_buffer_16
  Register #(.width(16)) Reg1 (.D(data_in), .en(controlled_buffer_1_out), .clk(Clock), .Q(Reg1_q), .clr(Reg_Reset));
  Register #(.width(16)) Reg2 (.D(data_in), .en(controlled_buffer_2_out), .clk(Clock), .Q(Reg2_q), .clr(Reg_Reset));
  Register #(.width(16)) Reg3 (.D(data_in), .en(controlled_buffer_3_out), .clk(Clock), .Q(Reg3_q), .clr(Reg_Reset));
  Register #(.width(16)) Reg4 (.D(data_in), .en(controlled_buffer_4_out), .clk(Clock), .Q(Reg4_q), .clr(Reg_Reset));
  not not_10 (not_10_out, OPcode[1]);
  not not_11 (not_11_out, OPcode[2]);
  not not_12 (not_12_out, OPcode[4]);
  assign data_out = controlled_buffer_5_out ? Reg1_q : 16'bz;  // Controlled_Buffer controlled_buffer_17
  assign data_out = controlled_buffer_6_out ? Reg2_q : 16'bz;  // Controlled_Buffer controlled_buffer_18
  assign data_out = controlled_buffer_7_out ? Reg3_q : 16'bz;  // Controlled_Buffer controlled_buffer_19
  and and_6 (and_6_out, OPcode[0], not_10_out, not_11_out, OPcode[3], not_12_out);
  assign data_out = controlled_buffer_8_out ? Reg4_q : 16'bz;  // Controlled_Buffer controlled_buffer_20
  not not_13 (not_13_out, OPcode[0]);
  not not_14 (not_14_out, OPcode[1]);
  not not_15 (not_15_out, OPcode[2]);
  not not_16 (not_16_out, OPcode[4]);
  and and_7 (and_7_out, not_13_out, not_14_out, not_15_out, OPcode[3], not_16_out);
  assign Reg1_out = and_6_out ? Reg1_q : 16'bz;  // Controlled_Buffer controlled_buffer_21
  assign Reg2_out = and_6_out ? Reg2_q : 16'bz;  // Controlled_Buffer controlled_buffer_22
  assign Reg3_out = and_6_out ? Reg3_q : 16'bz;  // Controlled_Buffer controlled_buffer_23
  assign Reg4_out = and_6_out ? Reg4_q : 16'bz;  // Controlled_Buffer controlled_buffer_24
  assign Block_store = and_7_out ? data_out : 16'bz;  // Controlled_Buffer controlled_buffer_25

  // Notes on the sheet:
  //   REG_SWAP
  //   MATMULT
endmodule

module Reg_bank_B (
  input  [15:0] Data_in,
  input  Clock,
  input  [4:0] Opcode,
  input  Flag,
  input  Reg5_WE,
  input  Reg6_WE,
  input  Reg7_WE,
  input  Reg8_WE,
  input  [4:0] Address,
  input  Reg5_CB,
  input  Reg6_CB,
  input  Reg7_CB,
  input  Reg8_CB,
  input  Reg_reset,
  output [15:0] Data_out,
  output [15:0] Block_store,
  output [15:0] Reg5_out,
  output [15:0] Reg6_out,
  output [15:0] Reg7_out,
  output [15:0] Reg8_out
);

  wire and_1_out, and_2_out, and_3_out, and_4_out, and_5_out, and_6_out, and_7_out, and_8_out,
       controlled_buffer_1_out, controlled_buffer_2_out, controlled_buffer_3_out, controlled_buffer_4_out,
       controlled_buffer_9_out, controlled_buffer_10_out, controlled_buffer_11_out, controlled_buffer_12_out,
       not_1_out, not_2_out, not_3_out, not_4_out, not_5_out, not_6_out, not_7_out, not_8_out, not_9_out,
       not_10_out, not_11_out, not_12_out, not_13_out, not_14_out, not_15_out, not_16_out;
  wire [15:0] Reg5_q, Reg6_q, Reg7_q, Reg8_q;

  not not_1 (not_1_out, Address[0]);
  not not_2 (not_2_out, Address[1]);
  not not_3 (not_3_out, Address[2]);
  not not_4 (not_4_out, Address[3]);
  not not_5 (not_5_out, Address[4]);
  not not_6 (not_6_out, Opcode[0]);
  not not_7 (not_7_out, Opcode[3]);
  not not_8 (not_8_out, Opcode[4]);
  assign controlled_buffer_1_out = and_1_out ? controlled_buffer_9_out : 1'bz;  // Controlled_Buffer controlled_buffer_1
  assign controlled_buffer_2_out = and_1_out ? controlled_buffer_10_out : 1'bz;  // Controlled_Buffer controlled_buffer_2
  assign controlled_buffer_3_out = and_1_out ? controlled_buffer_11_out : 1'bz;  // Controlled_Buffer controlled_buffer_3
  assign controlled_buffer_4_out = and_1_out ? controlled_buffer_12_out : 1'bz;  // Controlled_Buffer controlled_buffer_4
  and and_1 (and_1_out, not_6_out, Opcode[1], Opcode[2], not_7_out, not_8_out);
  and and_2 (and_2_out, Address[0], not_2_out, Address[2], not_4_out, not_5_out);
  and and_3 (and_3_out, not_1_out, Address[1], Address[2], not_4_out, not_5_out);
  and and_4 (and_4_out, Address[0], Address[1], Address[2], not_4_out, not_5_out);
  and and_5 (and_5_out, not_1_out, not_2_out, not_3_out, Address[3], not_5_out);
  assign controlled_buffer_1_out = not_9_out ? Reg5_WE : 1'bz;  // Controlled_Buffer controlled_buffer_5
  assign controlled_buffer_2_out = not_9_out ? Reg6_WE : 1'bz;  // Controlled_Buffer controlled_buffer_6
  assign controlled_buffer_3_out = not_9_out ? Reg7_WE : 1'bz;  // Controlled_Buffer controlled_buffer_7
  assign controlled_buffer_4_out = not_9_out ? Reg8_WE : 1'bz;  // Controlled_Buffer controlled_buffer_8
  not not_9 (not_9_out, and_1_out);
  assign controlled_buffer_9_out = and_1_out ? and_2_out : 1'bz;  // Controlled_Buffer controlled_buffer_9
  assign controlled_buffer_10_out = and_1_out ? and_3_out : 1'bz;  // Controlled_Buffer controlled_buffer_10
  assign controlled_buffer_11_out = and_1_out ? and_4_out : 1'bz;  // Controlled_Buffer controlled_buffer_11
  assign controlled_buffer_12_out = and_1_out ? and_5_out : 1'bz;  // Controlled_Buffer controlled_buffer_12
  assign controlled_buffer_9_out = not_9_out ? Reg5_CB : 1'bz;  // Controlled_Buffer controlled_buffer_13
  assign controlled_buffer_10_out = not_9_out ? Reg6_CB : 1'bz;  // Controlled_Buffer controlled_buffer_14
  assign controlled_buffer_11_out = not_9_out ? Reg7_CB : 1'bz;  // Controlled_Buffer controlled_buffer_15
  assign controlled_buffer_12_out = not_9_out ? Reg8_CB : 1'bz;  // Controlled_Buffer controlled_buffer_16
  Register #(.width(16)) Reg5 (.D(Data_in), .en(controlled_buffer_1_out), .clk(Clock), .Q(Reg5_q), .clr(Reg_reset));
  Register #(.width(16)) Reg6 (.D(Data_in), .en(controlled_buffer_2_out), .clk(Clock), .Q(Reg6_q), .clr(Reg_reset));
  Register #(.width(16)) Reg7 (.D(Data_in), .en(controlled_buffer_3_out), .clk(Clock), .Q(Reg7_q), .clr(Reg_reset));
  Register #(.width(16)) Reg8 (.D(Data_in), .en(controlled_buffer_4_out), .clk(Clock), .Q(Reg8_q), .clr(Reg_reset));
  not not_10 (not_10_out, Opcode[1]);
  not not_11 (not_11_out, Opcode[2]);
  not not_12 (not_12_out, Opcode[4]);
  assign Data_out = controlled_buffer_9_out ? Reg5_q : 16'bz;  // Controlled_Buffer controlled_buffer_17
  assign Data_out = controlled_buffer_10_out ? Reg6_q : 16'bz;  // Controlled_Buffer controlled_buffer_18
  assign Data_out = controlled_buffer_11_out ? Reg7_q : 16'bz;  // Controlled_Buffer controlled_buffer_19
  and and_6 (and_6_out, Opcode[0], not_10_out, not_11_out, Opcode[3], not_12_out);
  assign Data_out = controlled_buffer_12_out ? Reg8_q : 16'bz;  // Controlled_Buffer controlled_buffer_20
  not not_13 (not_13_out, Opcode[0]);
  not not_14 (not_14_out, Opcode[1]);
  not not_15 (not_15_out, Opcode[2]);
  not not_16 (not_16_out, Opcode[4]);
  and and_7 (and_7_out, not_13_out, not_14_out, not_15_out, Opcode[3], not_16_out);
  assign Reg5_out = and_6_out ? Reg5_q : 16'bz;  // Controlled_Buffer controlled_buffer_21
  assign Reg6_out = and_6_out ? Reg6_q : 16'bz;  // Controlled_Buffer controlled_buffer_22
  assign Reg7_out = and_6_out ? Reg7_q : 16'bz;  // Controlled_Buffer controlled_buffer_23
  assign Reg8_out = and_6_out ? Reg8_q : 16'bz;  // Controlled_Buffer controlled_buffer_24
  and and_8 (and_8_out, and_7_out, Flag);
  assign Block_store = and_8_out ? Data_out : 16'bz;  // Controlled_Buffer controlled_buffer_25

  // Notes on the sheet:
  //   REG_SWAP
  //   MATMULT
endmodule

module matmult (
  input  [4:0] OPcode,
  input  Flag,
  input  [15:0] a,
  input  [15:0] b,
  input  [15:0] c,
  input  [15:0] d,
  input  [15:0] e,
  input  [15:0] f,
  input  [15:0] g,
  input  [15:0] h,
  input  Clock,
  output [15:0] AE_BG,
  output [15:0] AF_BH,
  output [15:0] CE_DG,
  output [15:0] CF_DH,
  output [15:0] AE_BG_Overflow,
  output [15:0] AF_BH_Overflow,
  output [15:0] CE_DG_Overflow,
  output [15:0] CF_DH_Overflow,
  output Opcode_on
);

  wire and_2_out, and_3_out, and_4_out, and_5_out, and_6_out, and_7_out, and_8_out, controlled_buffer_11_out,
       controlled_buffer_12_out, controlled_buffer_15_out, controlled_buffer_16_out,
       controlled_buffer_19_out, controlled_buffer_20_out, controlled_buffer_23_out,
       controlled_buffer_24_out, not_1_out, not_2_out, not_3_out, not_4_out, not_5_out, not_6_out, not_7_out,
       not_8_out, not_9_out, not_10_out, not_11_out, not_12_out, not_13_out, not_14_out;
  wire [0:0] add_16bit_1_carry_out, add_16bit_2_carry_out, add_16bit_3_carry_out, add_16bit_4_carry_out;
  wire [4:0] counter_1_q;
  wire [7:0] controlled_buffer_1_out, controlled_buffer_2_out, controlled_buffer_3_out,
       controlled_buffer_4_out, controlled_buffer_5_out, controlled_buffer_6_out, controlled_buffer_7_out,
       controlled_buffer_8_out;
  wire [14:0] undriven, undriven_2, undriven_3, undriven_4;
  wire [15:0] add_16bit_1_sum_out, add_16bit_2_sum_out, add_16bit_3_sum_out, add_16bit_4_sum_out,
       mult_8_1_product, mult_8_2_product, mult_8_3_product, mult_8_4_product, mult_8_5_product,
       mult_8_6_product, mult_8_7_product, mult_8_8_product, register_1_q, register_2_q, register_3_q,
       register_4_q, register_5_q, register_6_q, register_7_q, register_8_q;

  not not_1 (not_1_out, OPcode[1]);
  not not_2 (not_2_out, OPcode[2]);
  not not_3 (not_3_out, OPcode[4]);
  and and_1 (Opcode_on, OPcode[0], not_1_out, not_2_out, OPcode[3], not_3_out);
  assign controlled_buffer_1_out = Opcode_on ? a[7:0] : 8'bz;  // Controlled_Buffer controlled_buffer_1
  assign controlled_buffer_2_out = Opcode_on ? b[7:0] : 8'bz;  // Controlled_Buffer controlled_buffer_2
  assign controlled_buffer_3_out = Opcode_on ? c[7:0] : 8'bz;  // Controlled_Buffer controlled_buffer_3
  assign controlled_buffer_4_out = Opcode_on ? d[7:0] : 8'bz;  // Controlled_Buffer controlled_buffer_4
  assign controlled_buffer_5_out = Opcode_on ? e[7:0] : 8'bz;  // Controlled_Buffer controlled_buffer_5
  assign controlled_buffer_6_out = Opcode_on ? f[7:0] : 8'bz;  // Controlled_Buffer controlled_buffer_6
  assign controlled_buffer_7_out = Opcode_on ? g[7:0] : 8'bz;  // Controlled_Buffer controlled_buffer_7
  assign controlled_buffer_8_out = Opcode_on ? h[7:0] : 8'bz;  // Controlled_Buffer controlled_buffer_8
  mult_8 mult_8_1 (.A(controlled_buffer_1_out), .B(controlled_buffer_5_out), .Product(mult_8_1_product));
  mult_8 mult_8_2 (.A(controlled_buffer_2_out), .B(controlled_buffer_7_out), .Product(mult_8_2_product));
  mult_8 mult_8_3 (.A(controlled_buffer_1_out), .B(controlled_buffer_6_out), .Product(mult_8_3_product));
  mult_8 mult_8_4 (.A(controlled_buffer_2_out), .B(controlled_buffer_8_out), .Product(mult_8_4_product));
  mult_8 mult_8_5 (.A(controlled_buffer_3_out), .B(controlled_buffer_5_out), .Product(mult_8_5_product));
  mult_8 mult_8_6 (.A(controlled_buffer_4_out), .B(controlled_buffer_7_out), .Product(mult_8_6_product));
  mult_8 mult_8_7 (.A(controlled_buffer_3_out), .B(controlled_buffer_6_out), .Product(mult_8_7_product));
  mult_8 mult_8_8 (.A(controlled_buffer_4_out), .B(controlled_buffer_8_out), .Product(mult_8_8_product));
  Counter #(.max('h1f), .width(5)) counter_1 (
    .clr(and_2_out), .up(Opcode_on), .count(Opcode_on), .clk(Clock), .Q(counter_1_q));  // open: load, D, carry
  and and_2 (and_2_out, counter_1_q[2], counter_1_q[0]);
  add_16bit add_16bit_1 (
    .A(mult_8_1_product), .B(mult_8_2_product), .sum_out(add_16bit_1_sum_out),
    .carry_out(add_16bit_1_carry_out[0]));  // open: carry_in
  add_16bit add_16bit_2 (
    .A(mult_8_3_product), .B(mult_8_4_product), .sum_out(add_16bit_2_sum_out),
    .carry_out(add_16bit_2_carry_out[0]));  // open: carry_in
  add_16bit add_16bit_3 (
    .A(mult_8_5_product), .B(mult_8_6_product), .sum_out(add_16bit_3_sum_out),
    .carry_out(add_16bit_3_carry_out[0]));  // open: carry_in
  add_16bit add_16bit_4 (
    .A(mult_8_7_product), .B(mult_8_8_product), .sum_out(add_16bit_4_sum_out),
    .carry_out(add_16bit_4_carry_out[0]));  // open: carry_in
  not not_4 (not_4_out, counter_1_q[0]);
  Register #(.width(16)) register_1 (
    .D(add_16bit_1_sum_out), .en(and_3_out), .clk(Clock), .Q(register_1_q));  // open: clr
  Register #(.width(16)) register_2 (
    .D({undriven, add_16bit_1_carry_out[0]}), .en(and_3_out), .clk(Clock), .Q(register_2_q));  // open: clr
  Register #(.width(16)) register_3 (
    .D(add_16bit_2_sum_out), .en(and_3_out), .clk(Clock), .Q(register_3_q));  // open: clr
  Register #(.width(16)) register_4 (
    .D({undriven_2, add_16bit_2_carry_out[0]}), .en(and_3_out), .clk(Clock), .Q(register_4_q));  // open: clr
  Register #(.width(16)) register_5 (
    .D(add_16bit_3_sum_out), .en(and_3_out), .clk(Clock), .Q(register_5_q));  // open: clr
  Register #(.width(16)) register_6 (
    .D({undriven_3, add_16bit_3_carry_out[0]}), .en(and_3_out), .clk(Clock), .Q(register_6_q));  // open: clr
  Register #(.width(16)) register_7 (
    .D(add_16bit_4_sum_out), .en(and_3_out), .clk(Clock), .Q(register_7_q));  // open: clr
  Register #(.width(16)) register_8 (
    .D({undriven_4, add_16bit_4_carry_out[0]}), .en(and_3_out), .clk(Clock), .Q(register_8_q));  // open: clr
  and and_3 (and_3_out, not_4_out, not_5_out, not_6_out);
  not not_5 (not_5_out, counter_1_q[1]);
  not not_6 (not_6_out, counter_1_q[2]);
  not not_7 (not_7_out, counter_1_q[0]);
  not not_8 (not_8_out, counter_1_q[0]);
  assign AE_BG = controlled_buffer_11_out ? register_1_q : 16'bz;  // Controlled_Buffer controlled_buffer_9
  assign AE_BG_Overflow = controlled_buffer_12_out ? register_2_q : 16'bz;  // Controlled_Buffer controlled_buffer_10
  assign controlled_buffer_11_out = and_8_out ? and_4_out : 1'bz;  // Controlled_Buffer controlled_buffer_11
  assign controlled_buffer_12_out = Flag ? and_4_out : 1'bz;  // Controlled_Buffer controlled_buffer_12
  and and_4 (and_4_out, counter_1_q[0], not_9_out, not_10_out);
  not not_9 (not_9_out, counter_1_q[1]);
  not not_10 (not_10_out, counter_1_q[2]);
  assign AF_BH = controlled_buffer_15_out ? register_3_q : 16'bz;  // Controlled_Buffer controlled_buffer_13
  assign AF_BH_Overflow = controlled_buffer_16_out ? register_4_q : 16'bz;  // Controlled_Buffer controlled_buffer_14
  assign controlled_buffer_15_out = and_8_out ? and_5_out : 1'bz;  // Controlled_Buffer controlled_buffer_15
  assign controlled_buffer_16_out = Flag ? and_5_out : 1'bz;  // Controlled_Buffer controlled_buffer_16
  and and_5 (and_5_out, not_7_out, counter_1_q[1], not_11_out);
  not not_11 (not_11_out, counter_1_q[2]);
  assign CE_DG = controlled_buffer_19_out ? register_5_q : 16'bz;  // Controlled_Buffer controlled_buffer_17
  assign CE_DG_Overflow = controlled_buffer_20_out ? register_6_q : 16'bz;  // Controlled_Buffer controlled_buffer_18
  assign controlled_buffer_19_out = and_8_out ? and_6_out : 1'bz;  // Controlled_Buffer controlled_buffer_19
  assign controlled_buffer_20_out = Flag ? and_6_out : 1'bz;  // Controlled_Buffer controlled_buffer_20
  and and_6 (and_6_out, counter_1_q[0], counter_1_q[1], not_12_out);
  not not_12 (not_12_out, counter_1_q[2]);
  assign CF_DH = controlled_buffer_23_out ? register_7_q : 16'bz;  // Controlled_Buffer controlled_buffer_21
  assign CF_DH_Overflow = controlled_buffer_24_out ? register_8_q : 16'bz;  // Controlled_Buffer controlled_buffer_22
  assign controlled_buffer_23_out = and_8_out ? and_7_out : 1'bz;  // Controlled_Buffer controlled_buffer_23
  assign controlled_buffer_24_out = Flag ? and_7_out : 1'bz;  // Controlled_Buffer controlled_buffer_24
  and and_7 (and_7_out, not_8_out, not_13_out, counter_1_q[2]);
  not not_13 (not_13_out, counter_1_q[1]);
  and and_8 (and_8_out, not_14_out, Opcode_on);
  not not_14 (not_14_out, Flag);

  // Notes on the sheet:
  //   AE
  //   BG
  //   AF
  //   BH
  //   CE
  //   DG
  //   CF
  //   DH
  //   AE+BG
  //   AF+BH
  //   CE+DG
  //   CF+DH
endmodule

module block_incrementer (
  input  [4:0] OPcode,
  input  [4:0] Address,
  input  Clock,
  output [4:0] inc_add
);

  wire and_1_out, not_1_out, not_2_out, not_3_out, not_4_out;
  wire [4:0] counter_1_q;
  wire [7:0] add_8bit_1_sum_out, counter_2_q;
  wire [7:5] undriven;

  Counter #(.max('h1f), .width(5)) counter_1 (
    .clr(not_1_out), .up(1'b1), .count(1'b1), .clk(Clock), .Q(counter_1_q));  // open: load, D, carry
  not not_1 (not_1_out, and_1_out);
  Counter #(.max('h1f), .width(5)) counter_2 (
    .clr(counter_2_q[2]), .up(counter_1_q[0]), .count(counter_1_q[0]), .clk(Clock), .Q(counter_2_q[4:0]));  // open: load, D, carry
  not not_2 (not_2_out, OPcode[3]);
  not not_3 (not_3_out, OPcode[4]);
  and and_1 (and_1_out, OPcode[0], OPcode[1], OPcode[2], not_2_out, not_3_out);
  not not_4 (not_4_out, and_1_out);
  assign inc_add = not_4_out ? Address : 5'bz;  // Controlled_Buffer controlled_buffer_1
  add_8bit add_8bit_1 (
    .A({undriven, Address}), .B(counter_2_q), .sum_out(add_8bit_1_sum_out));  // open: carry_in, carry_out
  // Probe on add_8bit_1_sum_out
  assign inc_add = and_1_out ? add_8bit_1_sum_out[4:0] : 5'bz;  // Controlled_Buffer controlled_buffer_2
  // Probe on inc_add
endmodule

module block_store_incrementer (
  input  [4:0] OPcode,
  input  [4:0] Address,
  input  Clock,
  output [4:0] inc_add,
  output Opcode_on
);

  wire not_1_out, not_2_out, not_3_out, not_4_out, not_5_out;
  wire [7:0] add_8bit_1_sum_out, counter_1_q;
  wire [7:5] undriven;

  not not_1 (not_1_out, OPcode[0]);
  not not_2 (not_2_out, OPcode[1]);
  not not_3 (not_3_out, OPcode[2]);
  not not_4 (not_4_out, OPcode[4]);
  Counter #(.max('h1f), .width(5)) counter_1 (
    .clr(counter_1_q[2]), .up(Opcode_on), .count(Opcode_on), .clk(Clock), .Q(counter_1_q[4:0]));  // open: load, D, carry
  and and_1 (Opcode_on, not_1_out, not_2_out, not_3_out, OPcode[3], not_4_out);
  not not_5 (not_5_out, Opcode_on);
  assign inc_add = not_5_out ? Address : 5'bz;  // Controlled_Buffer controlled_buffer_1
  add_8bit add_8bit_1 (
    .A({undriven, Address}), .B(counter_1_q), .sum_out(add_8bit_1_sum_out));  // open: carry_in, carry_out
  // Probe on add_8bit_1_sum_out
  assign inc_add = Opcode_on ? add_8bit_1_sum_out[4:0] : 5'bz;  // Controlled_Buffer controlled_buffer_2
  // Probe on inc_add
endmodule

module Busterminus (
  input  [4:0] Opcode,
  input  Flag,
  input  Clock,
  input  [4:0] Add_B,
  input  [4:0] Add_A,
  input  [15:0] Data_sys,
  input  [15:0] Data_A,
  input  [15:0] Data_B,
  output [4:0] Add_B_out,
  output [4:0] Add_A_out,
  output AddA_RamA,
  output AddA_RamB,
  output [15:0] Data_AB_Out,
  output [15:0] Data_SysA_Out,
  output Mem_swap,
  output Move_flag,
  output Move
);

  wire and_1_out, not_1_out, not_3_out, not_5_out, not_6_out, or_1_out, or_2_out, or_3_out, or_4_out,
       undriven;
  wire [4:0] counter_1_q;
  wire [15:0] controlled_buffer_1_out, controlled_buffer_3_out, Data_Reg1_q, Data_Reg2_q;

  not not_1 (not_1_out, Flag);
  // NOT_Gate not_2 has open pins: in=Opcode[0], out=open
  not not_3 (not_3_out, Opcode[1]);
  // NOT_Gate not_4 has open pins: in=Opcode[2], out=open
  not not_5 (not_5_out, Opcode[3]);
  not not_6 (not_6_out, Opcode[4]);
  and and_1 (and_1_out, Opcode[0], not_3_out, Opcode[2], not_5_out, not_6_out);
  and and_2 (AddA_RamB, Opcode[0], Opcode[1], Opcode[2], Opcode[3], not_6_out, Flag);
  and and_3 (AddA_RamA, Opcode[0], Opcode[1], Opcode[2], Opcode[3], not_6_out, not_1_out);
  or or_1 (or_1_out, and_1_out, AddA_RamB, AddA_RamA);
  or or_2 (or_2_out, AddA_RamB, AddA_RamA);
  or or_3 (or_3_out, and_1_out, AddA_RamB);
  or or_4 (or_4_out, AddA_RamB, AddA_RamA);
  assign controlled_buffer_1_out = or_2_out ? Data_sys : 16'bz;  // Controlled_Buffer controlled_buffer_1
  assign controlled_buffer_1_out = and_1_out ? Data_A : 16'bz;  // Controlled_Buffer controlled_buffer_2
  assign controlled_buffer_3_out = AddA_RamA ? Data_A : 16'bz;  // Controlled_Buffer controlled_buffer_3
  assign controlled_buffer_3_out = or_3_out ? Data_B : 16'bz;  // Controlled_Buffer controlled_buffer_4
  Counter #(.max('h1f), .width(5)) counter_1 (
    .clr(counter_1_q[2]), .up(and_1_out), .count(and_1_out), .clk(Clock), .Q(counter_1_q));  // open: load, D, carry
  assign Add_B_out = or_4_out ? Add_B : 5'bz;  // Controlled_Buffer controlled_buffer_5
  assign Add_A_out = or_4_out ? Add_A : 5'bz;  // Controlled_Buffer controlled_buffer_6
  Register #(.width(16)) Data_Reg1 (
    .D(controlled_buffer_1_out), .en(or_1_out), .clk(Clock), .Q(Data_Reg1_q));  // open: clr
  Register #(.width(16)) Data_Reg2 (
    .D(controlled_buffer_3_out), .en(or_1_out), .clk(Clock), .Q(Data_Reg2_q));  // open: clr
  assign Data_SysA_Out = or_1_out ? Data_Reg1_q : 16'bz;  // Controlled_Buffer controlled_buffer_7
  assign Data_AB_Out = or_1_out ? Data_Reg2_q : 16'bz;  // Controlled_Buffer controlled_buffer_8
  Register #(.width(5)) Add_Reg1 (.en(undriven));  // open: D, clk, Q, clr
  Register #(.width(5)) Add_Reg2 (.en(undriven));  // open: D, clk, Q, clr
  and and_4 (Mem_swap, counter_1_q[0], counter_1_q[1]);

  assign Move = AddA_RamA;
  assign Move_flag = AddA_RamB;
endmodule

module ALU (
  input  [15:0] A,
  input  [15:0] B,
  input  [4:0] opcode,
  input  flag,
  output [15:0] Result,
  output store,
  output [15:0] sto_overflow
);

  wire addsub_16bit_1_carry_out, and_1_out, and_3_out, decoder_5x16_1_add_sub, decoder_5x16_1_and1,
       decoder_5x16_1_block_load, decoder_5x16_1_block_store, decoder_5x16_1_compare,
       decoder_5x16_1_mem_swap, decoder_5x16_1_mult, decoder_5x16_1_nop_halt, decoder_5x16_1_not1,
       decoder_5x16_1_reg_swap, decoder_5x16_1_xor1;
  wire [15:0] addsub_16bit_1_sum_out, and_2_out, bit_extender_1_out, comparator_16bit_1_comparator_output,
       mult_8_1_product, not_1_out, xor_1_out;

  and and_1 (and_1_out, flag, decoder_5x16_1_add_sub);
  assign bit_extender_1_out = {{15{and_1_out}}, and_1_out};  // Bit_Extender bit_extender_1
  assign and_2_out = A & B;  // AND_Gate and_2, 16 bits wide
  assign xor_1_out = A ^ B;  // XOR_Gate xor_1, 16 bits wide
  assign not_1_out = ~A;  // NOT_Gate not_1, 16 bits wide
  addsub_16bit addsub_16bit_1 (
    .A(A), .B(B), .Carry_in(and_1_out), .Sub(bit_extender_1_out), .sum_out(addsub_16bit_1_sum_out),
    .carry_out(addsub_16bit_1_carry_out));
  mult_8 mult_8_1 (.A(A[7:0]), .B(B[7:0]), .Product(mult_8_1_product));
  comparator_16bit comparator_16bit_1 (.A(A), .B(B), .Comparator_output(comparator_16bit_1_comparator_output));
  decoder_5x16 decoder_5x16_1 (
    .in_1(opcode), .add_sub(decoder_5x16_1_add_sub), .Mult(decoder_5x16_1_mult), .STO_STO_OVERFLOW(store),
    .Mem_swap(decoder_5x16_1_mem_swap), .Reg_swap(decoder_5x16_1_reg_swap),
    .Block_load(decoder_5x16_1_block_load), .Block_store(decoder_5x16_1_block_store),
    .Compare(decoder_5x16_1_compare), .and1(decoder_5x16_1_and1), .xor1(decoder_5x16_1_xor1),
    .not1(decoder_5x16_1_not1), .nop_halt(decoder_5x16_1_nop_halt));  // open: Reserved, Mat_mult, Debug
  assign Result = decoder_5x16_1_add_sub ? addsub_16bit_1_sum_out : 16'bz;  // Controlled_Buffer controlled_buffer_1
  assign Result = decoder_5x16_1_mult ? mult_8_1_product : 16'bz;  // Controlled_Buffer controlled_buffer_2
  assign Result = decoder_5x16_1_compare ? comparator_16bit_1_comparator_output : 16'bz;  // Controlled_Buffer controlled_buffer_3
  assign sto_overflow[0] = and_3_out ? addsub_16bit_1_carry_out : 1'bz;  // Controlled_Buffer controlled_buffer_4
  and and_3 (and_3_out, flag, store);
  assign Result = decoder_5x16_1_and1 ? and_2_out : 16'bz;  // Controlled_Buffer controlled_buffer_5
  assign Result = decoder_5x16_1_xor1 ? xor_1_out : 16'bz;  // Controlled_Buffer controlled_buffer_6
  assign Result = decoder_5x16_1_not1 ? not_1_out : 16'bz;  // Controlled_Buffer controlled_buffer_7
endmodule

module halt (
  input  flag,
  input  [4:0] Opcode,
  output halt_inst
);

  wire not_1_out, not_2_out;

  not not_1 (not_1_out, Opcode[0]);
  not not_2 (not_2_out, Opcode[4]);
  nand nand_1 (halt_inst, flag, not_1_out, Opcode[1], Opcode[2], Opcode[3], not_2_out);
endmodule

module decoder_5x16 (
  input  [4:0] in_1,
  output Reserved,
  output add_sub,
  output Mult,
  output STO_STO_OVERFLOW,
  output Mem_swap,
  output Reg_swap,
  output Block_load,
  output Block_store,
  output Mat_mult,
  output Compare,
  output and1,
  output xor1,
  output not1,
  output nop_halt,
  output Debug
);

  wire not_1_out, not_2_out, not_3_out, not_4_out, not_5_out;

  not not_1 (not_1_out, in_1[4]);
  not not_2 (not_2_out, in_1[3]);
  not not_3 (not_3_out, in_1[2]);
  not not_4 (not_4_out, in_1[1]);
  not not_5 (not_5_out, in_1[0]);
  and and_1 (Reserved, not_1_out, not_2_out, not_3_out, not_4_out, not_5_out);
  and and_2 (add_sub, not_1_out, not_2_out, not_3_out, not_4_out, in_1[0]);
  and and_3 (Mult, not_1_out, not_2_out, not_3_out, in_1[1], in_1[0]);
  and and_4 (STO_STO_OVERFLOW, not_1_out, not_2_out, in_1[2], not_4_out, not_5_out);
  and and_5 (Mem_swap, not_1_out, not_2_out, in_1[2], not_4_out, in_1[0]);
  and and_6 (Reg_swap, not_1_out, not_2_out, in_1[2], in_1[1], not_5_out);
  and and_7 (Block_load, not_1_out, not_2_out, in_1[2], in_1[1], in_1[0]);
  and and_8 (Block_store, not_1_out, in_1[3], not_3_out, not_4_out, not_5_out);
  and and_9 (Mat_mult, not_1_out, in_1[3], not_3_out, not_4_out, in_1[0]);
  and and_10 (Compare, not_1_out, in_1[3], not_3_out, in_1[1], not_5_out);
  and and_11 (and1, not_1_out, in_1[3], not_3_out, in_1[1], in_1[0]);
  and and_12 (xor1, not_1_out, in_1[3], in_1[2], not_4_out, not_5_out);
  and and_13 (not1, not_1_out, in_1[3], in_1[2], not_4_out, in_1[0]);
  and and_14 (nop_halt, not_1_out, in_1[3], in_1[2], in_1[1], not_5_out);
  and and_15 (Debug, not_1_out, not_2_out, not_3_out, in_1[1], not_5_out);
endmodule

module comparator_16bit (
  input  [15:0] A,
  input  [15:0] B,
  output [15:0] Comparator_output
);

  wire addsub_16bit_1_carry_out, not_1_out, not_2_out, or_1_out;
  wire [15:0] addsub_16bit_1_sum_out, bit_extender_1_out, controlled_buffer_2_out;

  // Probe on A
  // Probe on B
  assign bit_extender_1_out = {{15{1'b1}}, 1'b1};  // Bit_Extender bit_extender_1
  // Probe on addsub_16bit_1_sum_out
  addsub_16bit addsub_16bit_1 (
    .A(A), .B(B), .Carry_in(1'b1), .Sub(bit_extender_1_out), .sum_out(addsub_16bit_1_sum_out),
    .carry_out(addsub_16bit_1_carry_out));
  not not_1 (not_1_out, addsub_16bit_1_carry_out);
  assign Comparator_output = not_1_out ? 16'h1 : 16'bz;  // Controlled_Buffer controlled_buffer_1
  or or_1 (or_1_out, addsub_16bit_1_sum_out[0], addsub_16bit_1_sum_out[1], addsub_16bit_1_sum_out[2], addsub_16bit_1_sum_out[3], addsub_16bit_1_sum_out[4], addsub_16bit_1_sum_out[5], addsub_16bit_1_sum_out[6], addsub_16bit_1_sum_out[7], addsub_16bit_1_sum_out[8], addsub_16bit_1_sum_out[9], addsub_16bit_1_sum_out[10], addsub_16bit_1_sum_out[11], addsub_16bit_1_sum_out[12], addsub_16bit_1_sum_out[13], addsub_16bit_1_sum_out[14], addsub_16bit_1_sum_out[15]);
  assign controlled_buffer_2_out = or_1_out ? 16'h4 : 16'bz;  // Controlled_Buffer controlled_buffer_2
  not not_2 (not_2_out, or_1_out);
  assign controlled_buffer_2_out = not_2_out ? 16'h2 : 16'bz;  // Controlled_Buffer controlled_buffer_3
  assign Comparator_output = addsub_16bit_1_carry_out ? controlled_buffer_2_out : 16'bz;  // Controlled_Buffer controlled_buffer_4
  // Probe on Comparator_output

  // Notes on the sheet:
  //   A
  //   B
  //   Result
endmodule

module split (
  input  [15:0] Instruction,
  input  write_enable,
  input  Clock,
  input  reset,
  output [4:0] Add_B,
  output [4:0] Add_A,
  output [4:0] Opcode,
  output flag
);

  Register #(.width(16)) register_1 (
    .D(Instruction), .en(write_enable), .clk(Clock), .Q({flag, Opcode, Add_A, Add_B}), .clr(reset));
endmodule

module add_2bit (
  input  A,
  input  B,
  input  Carry_in,
  output sum,
  output carry_out
);

  wire and_1_out, and_2_out, xor_1_out;

  xor xor_1 (xor_1_out, A, B);
  xor xor_2 (sum, xor_1_out, Carry_in);
  and and_1 (and_1_out, Carry_in, xor_1_out);
  and and_2 (and_2_out, A, B);
  LED led_1 (.in(sum));
  or or_1 (carry_out, and_1_out, and_2_out);
  LED led_2 (.in(carry_out));

  // Notes on the sheet:
  //   xor1
  //   xor2
  //   and1
  //   and2
  //   or1
endmodule

module add_4bit (
  input  [3:0] A,
  input  carry_in,
  input  [3:0] B,
  output [3:0] sum_out,
  output carry_out
);

  wire add_2bit_1_carry_out, add_2bit_2_carry_out, add_2bit_3_carry_out;

  // Probe on B
  // Probe on A
  LED led_1 (.in(carry_out));
  // Probe on sum_out
  add_2bit add_2bit_1 (.A(A[0]), .B(B[0]), .Carry_in(carry_in), .sum(sum_out[0]), .carry_out(add_2bit_1_carry_out));
  add_2bit add_2bit_2 (
    .A(A[1]), .B(B[1]), .Carry_in(add_2bit_1_carry_out), .sum(sum_out[1]), .carry_out(add_2bit_2_carry_out));
  add_2bit add_2bit_3 (
    .A(A[2]), .B(B[2]), .Carry_in(add_2bit_2_carry_out), .sum(sum_out[2]), .carry_out(add_2bit_3_carry_out));
  add_2bit add_2bit_4 (.A(A[3]), .B(B[3]), .Carry_in(add_2bit_3_carry_out), .sum(sum_out[3]), .carry_out(carry_out));

  // Notes on the sheet:
  //   c_out
endmodule

module add_8bit (
  input  [7:0] A,
  input  carry_in,
  input  [7:0] B,
  output [7:0] sum_out,
  output carry_out
);

  wire add_4bit_1_carry_out;

  // Probe on A
  // Probe on B
  add_4bit add_4bit_1 (
    .A(A[3:0]), .carry_in(carry_in), .B(B[3:0]), .sum_out(sum_out[3:0]), .carry_out(add_4bit_1_carry_out));
  add_4bit add_4bit_2 (
    .A(A[7:4]), .carry_in(add_4bit_1_carry_out), .B(B[7:4]), .sum_out(sum_out[7:4]), .carry_out(carry_out));
  LED led_1 (.in(carry_out));
  // Probe on sum_out
endmodule

module add_16bit (
  input  [15:0] A,
  input  carry_in,
  input  [15:0] B,
  output [15:0] sum_out,
  output carry_out
);

  wire add_8bit_1_carry_out;

  // Probe on A
  // Probe on B
  add_8bit add_8bit_1 (
    .A(A[7:0]), .carry_in(carry_in), .B(B[7:0]), .sum_out(sum_out[7:0]), .carry_out(add_8bit_1_carry_out));
  add_8bit add_8bit_2 (
    .A(A[15:8]), .carry_in(add_8bit_1_carry_out), .B(B[15:8]), .sum_out(sum_out[15:8]), .carry_out(carry_out));
  // Probe on sum_out
  LED led_1 (.in(carry_out));
endmodule

module addsub_8bit (
  input  [7:0] A,
  input  [7:0] B,
  input  Carry_in,
  input  [7:0] Sub,
  output [7:0] sum_out,
  output carry_out
);

  wire [7:0] xor_1_out;

  // Probe on A
  // Probe on B
  assign xor_1_out = B ^ Sub;  // XOR_Gate xor_1, 8 bits wide
  add_8bit add_8bit_1 (.A(A), .carry_in(Carry_in), .B(xor_1_out), .sum_out(sum_out), .carry_out(carry_out));
  // Probe on sum_out
  LED led_1 (.in(carry_out));

  // Notes on the sheet:
  //   rules: B must be bigger than A
  //   B is always the negative input
  //   this bit should be signed for subtractionand unsigned for addition
endmodule

module addsub_16bit (
  input  [15:0] A,
  input  [15:0] B,
  input  Carry_in,
  input  [15:0] Sub,
  output [15:0] sum_out,
  output carry_out
);

  wire [15:0] xor_1_out;

  // Probe on A
  // Probe on B
  assign xor_1_out = B ^ Sub;  // XOR_Gate xor_1, 16 bits wide
  add_16bit add_16bit_1 (.A(A), .carry_in(Carry_in), .B(xor_1_out), .sum_out(sum_out), .carry_out(carry_out));
  // Probe on sum_out
  LED led_1 (.in(carry_out));

  // Notes on the sheet:
  //   rules: B must be smaller than A
endmodule

module mult_4 (
  input  [3:0] B,
  input  [3:0] A,
  output [7:0] product
);

  wire [2:0] and_2_out;
  wire [3:0] and_5_out, and_9_out, and_13_out;
  wire [3:1] add_4bit_1_sum_out, add_4bit_2_sum_out;
  wire [3:3] add_4bit_1_carry_out, add_4bit_2_carry_out;

  // Probe on B
  // Probe on A
  and and_1 (product[0], B[0], A[0]);
  and and_2 (and_2_out[0], B[1], A[0]);
  and and_3 (and_2_out[1], B[2], A[0]);
  and and_4 (and_2_out[2], B[3], A[0]);
  and and_5 (and_5_out[0], B[0], A[1]);
  and and_6 (and_5_out[1], B[1], A[1]);
  and and_7 (and_5_out[2], B[2], A[1]);
  and and_8 (and_5_out[3], B[3], A[1]);
  and and_9 (and_9_out[0], B[0], A[2]);
  and and_10 (and_9_out[1], B[1], A[2]);
  and and_11 (and_9_out[2], B[2], A[2]);
  and and_12 (and_9_out[3], B[3], A[2]);
  and and_13 (and_13_out[0], B[0], A[3]);
  and and_14 (and_13_out[1], B[1], A[3]);
  and and_15 (and_13_out[2], B[2], A[3]);
  and and_16 (and_13_out[3], B[3], A[3]);
  add_4bit add_4bit_1 (
    .A({1'b0, and_2_out}), .carry_in(1'b0), .B(and_5_out), .sum_out({add_4bit_1_sum_out, product[1]}),
    .carry_out(add_4bit_1_carry_out[3]));
  add_4bit add_4bit_2 (
    .A({add_4bit_1_carry_out[3], add_4bit_1_sum_out}), .carry_in(1'b0), .B(and_9_out),
    .sum_out({add_4bit_2_sum_out, product[2]}), .carry_out(add_4bit_2_carry_out[3]));
  add_4bit add_4bit_3 (
    .A({add_4bit_2_carry_out[3], add_4bit_2_sum_out}), .carry_in(1'b0), .B(and_13_out),
    .sum_out(product[6:3]), .carry_out(product[7]));
  // Probe on product
endmodule

module mult_8 (
  input  [7:0] A,
  input  [7:0] B,
  output [15:0] Product
);

  wire [3:0] undriven_2, undriven_3, undriven_4, undriven_5;
  wire [7:0] mult_4_1_product, mult_4_2_product, mult_4_3_product, mult_4_4_product, undriven, undriven_6;
  wire [15:0] add_16bit_1_sum_out, add_16bit_2_sum_out;

  // Probe on A
  // Probe on B
  // Probe on mult_4_1_product
  mult_4 mult_4_1 (.B(B[3:0]), .A(A[3:0]), .product(mult_4_1_product));
  // Probe on mult_4_2_product
  mult_4 mult_4_2 (.B(B[7:4]), .A(A[3:0]), .product(mult_4_2_product));
  // Probe on mult_4_3_product
  mult_4 mult_4_3 (.B(B[3:0]), .A(A[7:4]), .product(mult_4_3_product));
  // Probe on mult_4_4_product
  mult_4 mult_4_4 (.B(B[7:4]), .A(A[7:4]), .product(mult_4_4_product));
  add_16bit add_16bit_1 (
    .A({undriven, mult_4_1_product}), .B({undriven_3, mult_4_2_product, undriven_2}),
    .sum_out(add_16bit_1_sum_out));  // open: carry_in, carry_out
  add_16bit add_16bit_2 (
    .A({undriven_5, mult_4_3_product, undriven_4}), .B({mult_4_4_product, undriven_6}),
    .sum_out(add_16bit_2_sum_out));  // open: carry_in, carry_out
  // Probe on add_16bit_1_sum_out
  // Probe on add_16bit_2_sum_out
  // Probe on Product
  add_16bit add_16bit_3 (
    .A(add_16bit_1_sum_out), .B(add_16bit_2_sum_out), .sum_out(Product));  // open: carry_in, carry_out
endmodule

module q (
  input  [4:0] in_1,
  input  in_2,
  input  in_3,
  input  in_4
);

  wire [15:0] controlled_buffer_1_out, ram_1_dout;

  RAM #(.addrWidth(5), .dataWidth(16)) ram_1 (.addr(in_1), .oe(in_3), .clk(in_2), .dout(ram_1_dout));  // open: we, din
  assign controlled_buffer_1_out = in_3 ? ram_1_dout : 16'bz;  // Controlled_Buffer controlled_buffer_1
  Register #(.width(16)) register_1 (.D(controlled_buffer_1_out), .en(in_4), .clk(in_2));  // open: Q, clr
endmodule
